# Fritzing sketch lsis1 (saved by Fritzing 0.9.9b)
breadboards: 1

parts:
  M1 = 5-ir-array-sensor [package=THT]
  M2 = >Wemos D1 R32  # not connected
  Componente1 = Motor Driver 1A Dual TB6612FNG
  DC_Mot_Enc1 = DC Motor with two-phase hall-encoder [part_number=VT-E-G25A-06-177E]
  DC_Mot_Enc2 = DC Motor with two-phase hall-encoder [part_number=VT-E-G25A-06-177E]
  Mod1 = KY-018 Photoresistor Module [package="Breakout board"]
  Mod2 = Arduino Sensor Shield v5.0
  Bat1 = battery_holder_dual_18650 [part_number=TBH-18650-2A-P]
  JACK1 = 2.1mm Barrel Jack with Terminal Block

nets:
  N1: M1.S5, Mod2.A5-SIG
  N2: M1.S4, Mod2.A4-SIG, Mod2.IIC-SDA, Mod2.APC220-
  N3: M1.S3, Mod2.A3-SIG
  N4: M1.S2, Mod2.A2-SIG
  N5: M1.S1, Mod2.URF01-A1, Mod2.A1-SIG
  GND: M1.GND, Componente1.GND, DC_Mot_Enc1.pin5, DC_Mot_Enc2.pin5, Mod1.-, Mod2.SD-D10
  VCC: M1.VCC, Componente1.VCC, DC_Mot_Enc1.pin2, DC_Mot_Enc2.pin2, DC_Mot_Enc2.pin3, Mod1.Vin, Mod2.SD-D11, Mod2.11-S
  N6: Componente1.B01, DC_Mot_Enc1.pin1
  N7: Componente1.B02, DC_Mot_Enc1.pin6
  N8: Componente1.A02, DC_Mot_Enc2.pin1
  N9: Componente1.A01, DC_Mot_Enc2.pin6
  N10: Componente1.PWMA, Mod2.8-S, Mod2.ParallelLCD-D8
  N11: Componente1.AIN2, Mod2.7-S, Mod2.ParallelLCD-D7
  N12: Componente1.AIN1, Mod2.6-S, Mod2.ParallelLCD-D6
  N13: Componente1.STBY, Mod2.5-S, Mod2.ParallelLCD-D5
  N14: Componente1.BIN1, Mod2.4-S, Mod2.ParallelLCD-D4
  N15: Componente1.BIN2, Mod2.3-S, Mod2.ParallelLCD-D3
  N16: Componente1.PWMB, Mod2.2-S, Mod2.ParallelLCD-D2
  N17: DC_Mot_Enc1.pin3, Mod2.13-S, Mod2.ParallelLCD-D13
  N18: DC_Mot_Enc1.pin4, Mod2.12-S, Mod2.ParallelLCD-D12
  N19: DC_Mot_Enc2.pin4, Mod2.10-S, Mod2.ParallelLCD-D10
  N20: Mod1.S, Mod2.URF01-A0, Mod2.A0-SIG
  N21: Bat1.+#0, JACK1.POS
  N22: Bat1.+#2, JACK1.NEG

custom parts:
  5-ir-array-sensor: 5 IR array sensor.
  >Wemos D1 R32: Wemos D1 R32 - This board is used with dual-mode Wi-Fi and Bluetooth chips, which is safe, reliable, and scalable to a variety of applications. DC in 5V-12V, 1 analog input(3.2V max input), a Micro USB connection, Compatible with D1 R32=WiFi+bluetooth+UNO
  KY-018 Photoresistor Module: KY-018 Photoresistor module, used to measure light intensity. It can determine the presence or absence of light.
  battery_holder_dual_18650: TBH-18650-2A-P dual 18650 battery holder.
